# Fritzing sketch 6-2 (saved by Fritzing 0.9.4)
breadboards: 1

parts:
  T1 = LM35 Temperature Sensor [package="TO92 [THT]"]
  LED1 = LED - 5mm [color="Red (633nm)" package="5 mm [THT]"]
  R1 = Resistor [tolerance=±5% resistance=220 package=THT]
  Part1 = Arduino Uno (Rev3)

nets:
  N1: T1.+Vs, Part1.5V
  N2: T1.Vout, Part1.A0
  GND: T1.GND, R1.Pin_1, Part1.GND
  N3: LED1.cathode, Part1.D9_PWM
  N4: LED1.anode, R1.Pin_0
